// Digital circuit mode_selector.dig as structural Verilog
module mode_selector (
  input  ID,
  input  PWD,
  input  DIS,
  input  RESET,
  input  CLK,
  input  RST,
  output IDO,
  output PWDO
);

  wire and_1_out, and_2_out, and_3_out, and_4_out, not_1_out, not_2_out, not_3_out, or_1_out, or_2_out;

  not not_1 (not_1_out, DIS);
  not not_2 (not_2_out, RST);
  and and_1 (and_1_out, ID, not_1_out);
  and and_2 (and_2_out, PWD, not_1_out);
  or or_1 (or_1_out, not_2_out, RESET);
  not not_3 (not_3_out, and_1_out);
  and and_3 (and_3_out, PWDO, not_3_out);
  and and_4 (and_4_out, not_3_out, and_2_out);
  or or_2 (or_2_out, and_3_out, and_4_out);
  D_FF_AS d_ff_as_1 (.Set(1'b0), .D(or_2_out), .C(CLK), .Clr(or_1_out), .Q(PWDO), .nQ(IDO));

  // Notes on the sheet:
  //   Zeynep Türkmen - 29541,
  //   Emre Kaan Usta - 30728
endmodule
